# Fritzing sketch 红外控制LED灯 (saved by Fritzing 0.9.4)
breadboards: 1

parts:
  元件1 = Arduino Nano (Rev3.0)
  R1 = Resistor [tolerance=±5% resistance=220 package=THT]
  LED1 = LED - 5mm [color="Red (633nm)" package="5 mm [THT]"]
  IR1 = TSOP312.., 314.. [package=THT]
  R2 = Resistor [tolerance=±5% resistance=220 package=THT]

nets:
  GND: 元件1.GND, LED1.cathode, IR1.GND
  N1: 元件1.D11/MOSI, R1.Pin_1, IR1.Data
  N2: 元件1.5V, R1.Pin_0, IR1.Vs
  N3: 元件1.D13/SCK, R2.Pin_1
  N4: LED1.anode, R2.Pin_0
